# Fritzing sketch Controller (saved by Fritzing 0.9.3b)
breadboards: 1

parts:
  Part1 = Arduino Nano (Rev3.0)  # not connected
  Part2 = Thumb Joystick
  GY1 = MPU-6050 Board GY-521 [form="♀ (female)" package=THT]
  Part3 = NRF24L01+ Breakout Board

nets:
  N1: Part2.GND, Part2.SEL, GY1.pin2
  VCC: Part2.VCC, GY1.pin1, Part3.VCC

custom parts:
  MPU-6050 Board GY-521: Acelerometro y Giroscopio MPU-6050 Board GY-521
